# Fritzing sketch Beat707_BigTime (saved by Fritzing 0.4.3b)
breadboards: 1

parts:
  SV3 = female pin header, 4 pins [form="♀ (female)"]
  J1 = female pin header, 4 pins [form="♀ (female)"]
  U1 = 74HC595 [package="DIP16 [THT]"]
  ATtiny85 = IC, DIP package, 8 pins [chip_label=A-85 spacing=300mil]
  Multiplexer = IC, DIP package, 24 pins [chip_label=CD4067 spacing=300mil]
  7_Segment_Clock_LED = IC, DIP package, 12 pins [spacing=300mil]
  SV1 = female pin header, 4 pins [form="♀ (female)"]  # not connected
  J1_2 = female pin header, 4 pins [form="♀ (female)"]
  R2 = Resistor [resistance=100 package=THT]

nets:
  N1: SV3.pin2, ATtiny85.pin5
  N2: SV3.pin3, ATtiny85.pin7
  N3: J1.pin1, U1.GND, U1.OE, ATtiny85.pin4, Multiplexer.pin12, Multiplexer.pin15, R2.Pin_0
  N4: U1.Q1, Multiplexer.pin11
  N5: U1.Q2, Multiplexer.pin14
  N6: U1.Q3, Multiplexer.pin13
  N7: U1.Q4, 7_Segment_Clock_LED.pin12
  N8: U1.Q5, 7_Segment_Clock_LED.pin9
  N9: U1.Q6, 7_Segment_Clock_LED.pin8
  N10: U1.Q7, 7_Segment_Clock_LED.pin6
  N11: U1.MR, U1.VCC, ATtiny85.pin8, Multiplexer.pin24, J1_2.pin4
  N12: U1.SH_CP, ATtiny85.pin2
  N13: U1.ST_CP, ATtiny85.pin6
  N14: U1.DS, ATtiny85.pin3
  N15: U1.Q0, Multiplexer.pin10
  N16: Multiplexer.pin1, R2.Pin_1
  N17: Multiplexer.pin2, 7_Segment_Clock_LED.pin3
  N18: Multiplexer.pin3, 7_Segment_Clock_LED.pin5
  N19: Multiplexer.pin4, 7_Segment_Clock_LED.pin10
  N20: Multiplexer.pin5, 7_Segment_Clock_LED.pin1
  N21: Multiplexer.pin6, 7_Segment_Clock_LED.pin2
  N22: Multiplexer.pin7, 7_Segment_Clock_LED.pin4
  N23: Multiplexer.pin8, 7_Segment_Clock_LED.pin7
  N24: Multiplexer.pin9, 7_Segment_Clock_LED.pin11
