# Fritzing sketch Hack_001_AnalogInputMode (saved by Fritzing 0.4.3b)
breadboards: 1

parts:
  R1 = Rotary Potentiometer (Large) [package=THT]
  S1 = Pushbutton [package=THT]
  Beat707_SV2_Header = female pin header, 4 pins [form="♀ (female)"]
  J1 = female pin header, 4 pins [form="♀ (female)"]  # not connected
  SV3 = female pin header, 4 pins [form="♀ (female)"]  # not connected
  J1_2 = female pin header, 4 pins [form="♀ (female)"]
  J1_3 = female pin header, 4 pins [form="♀ (female)"]
  SV1 = female pin header, 4 pins [form="♀ (female)"]  # not connected

nets:
  N1: R1.leg1, S1.Pin_1, S1.Pin_2, J1_2.pin1
  N2: R1.wiper, Beat707_SV2_Header.pin1
  N3: R1.leg2, J1_3.pin4
  N4: S1.Pin_3, S1.Pin_4, J1_2.pin4
