# Fritzing sketch Beat707 MPU (saved by Fritzing 0.9.3b)
circuit board: 5.37143cm x 1.61409cm
breadboards: 1

parts:
  U1 = IC, DIP package, 20 pins [chip_label=ATtiny2313]
  GND_VCC_TXD = female pin header, 3 pins [form="♀ (female)"]
  LED = smd LED [color="Red (633nm)" package="0805 [SMD]"]
  1K(0805) = Resistor [tolerance=±5% resistance=1k package="0805 [SMD]"]
  Button = Pushbutton [package="[THT]"]
  GND_VCC_RXD = female pin header, 3 pins [form="♀ (female)"]
  10K = Resistor [tolerance=±5% resistance=10k package="0805 [SMD]"]
  100nF = Ceramic Capacitor [capacitance=100nF package="0805 [SMD, multilayer]"]

nets:
  N1: U1.pin1, 10K.Pin_1
  N2: U1.pin2, GND_VCC_RXD.pin3
  N3: U1.pin3, GND_VCC_TXD.pin3
  N4: U1.pin4, 1K(0805).Pin_0
  N5: U1.pin5, Button.Pin_3, Button.Pin_4
  N6: U1.pin10, GND_VCC_TXD.pin1, LED.cathode, Button.Pin_1, Button.Pin_2, GND_VCC_RXD.pin1, 100nF.1
  N7: U1.pin20, GND_VCC_TXD.pin2, GND_VCC_RXD.pin2, 10K.Pin_0, 100nF.0
  N8: LED.anode, 1K(0805).Pin_1

notes:
  MIDI Input
  MIDI Output
  We are not using an octopler since we are powering the ATtiny directly from the MIDI power. This is a Hack, going outside the MIDI specs bounds. But works fine as the ATtiny is a low powered device.
  1
  +
  GND
  VCC
  RXD
  TXD
  Beat707.com MPU
