# Fritzing sketch Beat707 Mikro V2 (saved by Fritzing 0.9.3b)
circuit board: 10cm x 10cm
breadboards: 5

parts:
  atMega328_IC_#2 = atmega328 [package=dip]
  10k = Resistor [tolerance=±5% resistance=10k package=THT]
  C1 = Electrolytic Capacitor [capacitance=1µF package="100 mil [THT, electrolytic]"]
  FTDI_IC_#2 = male pin header, 6 pins [form="♂ (male)"]
  SD_Card_(CS_Pin_10) = female pin header, 8 pins [form="♀ (female)"]
  SD_Card1 = female pin header, 8 pins [form="♀ (female)"]
  Interface_Headers = shrouded pin header, 16 pins [form="♂ (shrouded male)"]
  2IC = female pin header, 4 pins [form="♀ (female)"]
  10k_2 = Resistor [tolerance=±5% resistance=10k package=THT]
  10k_3 = Resistor [tolerance=±5% resistance=10k package=THT]
  FTDI_IC_#1 = male pin header, 6 pins [form="♂ (male)"]
  atMega328_IC_#1 = atmega328 [part_number=IC2 package=dip]
  10k_4 = Resistor [tolerance=±5% resistance=10k package=THT]
  MIDI_Output = MIDI_CONN_FEMALE_SUPPORT [part_number="MIDI Output" package=din_5_female_support]
  220 = Resistor [tolerance=±5% resistance=220 package=THT]
  MIDI_Out = female pin header, 2 pins [form="♀ (female)"]
  MIDI_Input = MIDI_CONN_FEMALE_SUPPORT [part_number="MIDI Input" package=din_5_female_support]
  MIDI_In = female pin header, 2 pins [form="♀ (female)"]
  1N4748 = Rectifier Diode [part_number=1N4748 package="300 mil [THT]"]
  220_2 = Resistor [tolerance=±5% resistance=220 part_number=O1 package=THT]
  1k = Resistor [tolerance=±5% resistance=1k package=THT]
  220_3 = Resistor [tolerance=±5% resistance=220 part_number=O1 package=THT]
  USB_D_In = female pin header, 2 pins [form="♀ (female)"]
  USB_D_Out = female pin header, 2 pins [form="♀ (female)"]
  100nF = Ceramic Capacitor [capacitance=100nF package="100 mil [THT, multilayer]"]
  100nF_2 = Ceramic Capacitor [capacitance=100nF package="200 mil [THT, multilayer]"]
  100nF_3 = Ceramic Capacitor [capacitance=100nF package="200 mil [THT, multilayer]"]
  100nF_4 = Ceramic Capacitor [capacitance=100nF package="200 mil [THT, multilayer]"]
  CONN1 = USB connector [package=THT]
  X1 = USB Connectors [package=usb-a-h]
  Extras = female pin header, 9 pins [form="♀ (female)"]
  Extras_2 = female pin header, 5 pins [form="♀ (female)"]
  A3 = female pin header, 4 pins [form="♀ (female)"]
  Power_Switch = female pin header, 2 pins [form="♀ (female)"]
  4N35 = Optocoupler [package=THT]
  16mhz = CRYSTAL [part_number=16mhz package=hc49u-v]
  22pf = Ceramic Capacitor [capacitance=100nF package="100 mil [THT, multilayer]"]
  22pf_2 = Ceramic Capacitor [capacitance=100nF package="100 mil [THT, multilayer]"]
  16mhz_2 = CRYSTAL [part_number=16mhz package=hc49u-v]
  22pf1 = Ceramic Capacitor [capacitance=100nF package="100 mil [THT, multilayer]"]
  22pf_3 = Ceramic Capacitor [capacitance=100nF package="100 mil [THT, multilayer]"]
  Vox1k = Resistor [tolerance=±5% resistance=10k package=THT]
  10k2 = Resistor [tolerance=±5% resistance=10k package=THT]
  Vox1k_2 = Resistor [tolerance=±5% resistance=10k package=THT]
  Vox_Audio = female pin header, 4 pins [form="♀ (female)"]
  Vox_Cntrl = female pin header, 4 pins [form="♀ (female)"]

nets:
  N1: atMega328_IC_#2.RESET, 10k.Pin_1, 100nF_3.1
  N2: atMega328_IC_#2.D0_(RX), FTDI_IC_#2.pin4
  N3: atMega328_IC_#2.D1_(TX), FTDI_IC_#2.pin5
  N4: atMega328_IC_#2.D2, Interface_Headers.pin8
  N5: atMega328_IC_#2.D3_(PWM), Interface_Headers.pin7
  N6: atMega328_IC_#2.D4, Interface_Headers.pin6
  VCC: atMega328_IC_#2.VCC, atMega328_IC_#2.AVCC, atMega328_IC_#2.AREF, 10k.Pin_0, C1.+, FTDI_IC_#2.pin3, SD_Card_(CS_Pin_10).pin3, SD_Card1.pin3, Interface_Headers.pin10, Interface_Headers.pin11, 2IC.pin2, 10k_2.Pin_1, 10k_3.Pin_1, FTDI_IC_#1.pin3, atMega328_IC_#1.VCC, atMega328_IC_#1.AVCC, atMega328_IC_#1.AREF, 10k_4.Pin_0, 220.Pin_1, 1k.Pin_1, 100nF.1, 100nF_4.1, X1.VBUS, Power_Switch.pin1, Vox_Cntrl.pin4
  GND: atMega328_IC_#2.GND, C1.-, FTDI_IC_#2.pin1, SD_Card_(CS_Pin_10).pin1, SD_Card1.pin1, Interface_Headers.pin9, 2IC.pin1, FTDI_IC_#1.pin1, atMega328_IC_#1.GND, MIDI_Output.NC1, 220_3.Pin_0, 100nF.0, 100nF_4.0, CONN1.GND, CONN1.chassis5, CONN1.chassis6, X1.GND, Extras.pin4, Extras.pin5, 4N35.Pin_4, 22pf.1, 22pf_2.0, 22pf1.1, 22pf_3.0, Vox_Audio.pin1, Vox_Cntrl.pin1
  N7: atMega328_IC_#2.XLAT1, 16mhz_2.1, 22pf_3.1
  N8: atMega328_IC_#2.XLAT2, 16mhz_2.2, 22pf1.0
  N9: atMega328_IC_#2.D5_(PWM), Interface_Headers.pin3
  N10: atMega328_IC_#2.D6_(PWM), Interface_Headers.pin2
  N11: atMega328_IC_#2.D7, Interface_Headers.pin1
  N12: atMega328_IC_#2.D8, Interface_Headers.pin16
  N13: atMega328_IC_#2.D9_(PWM), Vox1k_2.Pin_0
  N14: atMega328_IC_#2.D10_(PWM), SD_Card_(CS_Pin_10).pin4, SD_Card1.pin4
  N15: atMega328_IC_#2.D11_(PWM), SD_Card_(CS_Pin_10).pin5, SD_Card1.pin5
  N16: atMega328_IC_#2.D12, SD_Card_(CS_Pin_10).pin7, SD_Card1.pin7
  N17: atMega328_IC_#2.D13, SD_Card_(CS_Pin_10).pin6, SD_Card1.pin6
  N18: atMega328_IC_#2.A0, Interface_Headers.pin12
  N19: atMega328_IC_#2.A1, Interface_Headers.pin13
  N20: atMega328_IC_#2.A2, Interface_Headers.pin14
  N21: atMega328_IC_#2.A3, Interface_Headers.pin15
  N22: atMega328_IC_#2.A4, Interface_Headers.pin5, 2IC.pin3, 10k_3.Pin_0, atMega328_IC_#1.A4
  N23: atMega328_IC_#2.A5, Interface_Headers.pin4, 2IC.pin4, 10k_2.Pin_0, atMega328_IC_#1.A5
  N24: FTDI_IC_#2.pin6, 100nF_3.0
  N25: SD_Card_(CS_Pin_10).pin2, SD_Card1.pin2
  N26: SD_Card_(CS_Pin_10).pin8, SD_Card1.pin8
  N27: FTDI_IC_#1.pin4, atMega328_IC_#1.D0_(RX), MIDI_In.pin2, USB_D_In.pin1
  N28: FTDI_IC_#1.pin5, atMega328_IC_#1.D1_(TX), MIDI_Out.pin1, USB_D_Out.pin1
  N29: FTDI_IC_#1.pin6, 100nF_2.0
  N30: atMega328_IC_#1.RESET, 10k_4.Pin_1, 100nF_2.1
  N31: atMega328_IC_#1.D2, Extras.pin1
  N32: atMega328_IC_#1.D3_(PWM), Extras.pin2
  N33: atMega328_IC_#1.D4, Extras.pin3
  N34: atMega328_IC_#1.XLAT1, 16mhz.1, 22pf_2.1
  N35: atMega328_IC_#1.XLAT2, 16mhz.2, 22pf.0
  N36: atMega328_IC_#1.D5_(PWM), Extras.pin6
  N37: atMega328_IC_#1.D6_(PWM), Extras.pin7
  N38: atMega328_IC_#1.D7, Extras.pin8
  N39: atMega328_IC_#1.D8, Extras.pin9, Vox_Cntrl.pin3
  N40: atMega328_IC_#1.D9_(PWM), Extras_2.pin5, Vox1k.Pin_0
  N41: atMega328_IC_#1.D10_(PWM), Extras_2.pin4, 10k2.Pin_0
  N42: atMega328_IC_#1.D11_(PWM), Extras_2.pin3
  N43: atMega328_IC_#1.D12, Extras_2.pin2
  N44: atMega328_IC_#1.D13, Extras_2.pin1
  N45: atMega328_IC_#1.A0, A3.pin4, Vox_Cntrl.pin2
  N46: atMega328_IC_#1.A1, A3.pin3
  N47: atMega328_IC_#1.A2, A3.pin2
  N48: atMega328_IC_#1.A3, A3.pin1
  N49: MIDI_Output.MIDI_IN, MIDI_Out.pin2
  N50: MIDI_Output.MIDI_OUT, 220.Pin_0
  N51: MIDI_Input.MIDI_IN, 220_2.Pin_1
  N52: MIDI_Input.MIDI_OUT, 1N4748.anode, 4N35.Pin_2
  N53: MIDI_In.pin1, 1k.Pin_0, 4N35.Pin_5
  N54: 1N4748.cathode, 220_2.Pin_0, 4N35.Pin_1
  N55: 220_3.Pin_1, 4N35.Pin_6
  N56: USB_D_In.pin2, CONN1.d+
  N57: USB_D_Out.pin2, X1.D+
  N58: CONN1.5V, Power_Switch.pin2
  N59: Vox1k.Pin_1, Vox_Audio.pin2
  N60: 10k2.Pin_1, Vox_Audio.pin3
  N61: Vox1k_2.Pin_1, Vox_Audio.pin4

notes:
  GND
  MISO
  VCC
  RST
  SCL
  Beat707.com
  Wusik.com
  (c) 2017
  1
  D2
  D8
  A0
  D13
  D9
  Version 2.0
