# Fritzing sketch Beat707 Playa (saved by Fritzing 0.9.3b)
circuit board: 10cm x 6.4cm
breadboards: 2

parts:
  ATMega328 = atmega328 [package=dip]
  16MHz = Crystal [frequency="16 Mhz" package=THT]
  C1 = Ceramic Capacitor [capacitance=22pF package="100 mil [THT, multilayer]"]
  22pf = Ceramic Capacitor [capacitance=22pF package="100 mil [THT, multilayer]"]
  100k = Resistor [tolerance=±5% resistance=10k package=THT]
  W25Q64 = IC, DIP package, 8 pins [chip_label=W25Q64]
  CD4050 = IC, DIP package, 16 pins [chip_label=CD4050]
  Reset = Pushbutton [package="[THT]"]
  100nf = Ceramic Capacitor [capacitance=100nF package="100 mil [THT, multilayer]"]
  100nf_2 = Ceramic Capacitor [capacitance=100nF package="100 mil [THT, multilayer]"]
  10uf = Electrolytic Capacitor [capacitance=10µF package="100 mil [THT, electrolytic]"]
  USB_5V = USB Connectors [package=usb-b-pth]
  LM317 = Voltage Regulator - Variable [package="TO220 [THT]"]
  470 = Resistor [tolerance=±5% resistance=470 package=THT]
  75 = Resistor [tolerance=±5% resistance=75 package=THT]
  100uf = Electrolytic Capacitor [capacitance=100µF package="100 mil [THT, electrolytic]"]
  330 = Resistor [tolerance=±5% resistance=330 package=THT]
  100nf_3 = Ceramic Capacitor [capacitance=100nF package="100 mil [THT, multilayer]"]
  R1 = Trimmer Potentiometer [maximum_resistance=10kΩ package=THT]
  100nf_4 = Ceramic Capacitor [capacitance=100nF package="100 mil [THT, multilayer]"]
  Audio_Out = female pin header, 2 pins [form="♀ (female)"]

nets:
  N1: ATMega328.RESET, 100k.Pin_1, Reset.Pin_3, Reset.Pin_4
  N2: ATMega328.VCC, ATMega328.AVCC, ATMega328.AREF, 100k.Pin_0, 100nf.1, USB_5V.VBUS, LM317.IN, 100uf.+
  GND: ATMega328.GND, C1.0, 22pf.0, W25Q64.pin4, CD4050.pin8, Reset.Pin_1, Reset.Pin_2, 100nf.0, 100nf_2.0, 10uf.-, USB_5V.GND, 470.Pin_0, 100uf.-, 100nf_3.0, Audio_Out.pin2
  N3: ATMega328.XLAT1, 16MHz.pin_0, C1.1
  N4: ATMega328.XLAT2, 16MHz.pin_1, 22pf.1
  N5: ATMega328.D8, CD4050.pin3
  N6: ATMega328.D9_(PWM), 100nf_4.0
  N7: ATMega328.D11_(PWM), CD4050.pin7
  N8: ATMega328.D12, W25Q64.pin2
  N9: ATMega328.D13, CD4050.pin5
  N10: W25Q64.pin1, CD4050.pin2
  N11: W25Q64.pin3, W25Q64.pin7, W25Q64.pin8, CD4050.pin1, 100nf_2.1, 10uf.+, LM317.OUT, 330.Pin_1, 100nf_3.1
  N12: W25Q64.pin5, CD4050.pin6
  N13: W25Q64.pin6, CD4050.pin4
  N14: LM317.ADJ, 75.Pin_0, 330.Pin_0
  N15: 470.Pin_1, 75.Pin_1
  N16: R1.leg1, 100nf_4.1
  N17: R1.wiper, Audio_Out.pin1

notes:
  3.3V
  5V
  Audio Out
