# Fritzing sketch Beat707_SY_LE (saved by Fritzing 0.6.2b)
breadboards: 2

parts:
  Optocoupler_-_Isolator = Optocoupler [package=THT]
  Arduino1 = Arduino
  R1 = Resistor [tolerance=±5% resistance=10k package=THT]
  R2 = Resistor [tolerance=±5% resistance=10k package=THT]
  R3 = Resistor [tolerance=±5% resistance=10k package=THT]
  R4 = Resistor [tolerance=±5% resistance=10k package=THT]
  R5 = Resistor [tolerance=±5% resistance=10k package=THT]
  R6 = Resistor [tolerance=±5% resistance=10k package=THT]
  R7 = Resistor [tolerance=±5% resistance=10k package=THT]
  part = Resistor [tolerance=±5% resistance=10k package=THT]
  Audio-Output = Stereo Jack (TRS) 3.5mm [package="PG203J [THT]"]
  part_2 = Resistor [tolerance=±5% resistance=100k package=THT]
  part_3 = Resistor [tolerance=±5% resistance=3.3k package=THT]
  Midi_Input = DIN-5 jack (MIDI) [package=THT]
  part_4 = Resistor [tolerance=±5% resistance=220 package=THT]

nets:
  N1: Optocoupler_-_Isolator.Pin_1, part_4.Pin_1
  N2: Optocoupler_-_Isolator.Pin_2, Midi_Input.4
  N3: Optocoupler_-_Isolator.Pin_4, Arduino1.GND, Audio-Output.Sleeve, part_2.Pin_1
  N4: Optocoupler_-_Isolator.Pin_5, Arduino1.D0RX, part_3.Pin_0
  N5: Optocoupler_-_Isolator.Pin_6, part_2.Pin_0
  N6: Arduino1.D9, R1.Pin_0
  N7: Arduino1.D8, R2.Pin_0
  N8: Arduino1.D7, R3.Pin_0
  N9: Arduino1.D6, R4.Pin_0
  N10: Arduino1.D5, R6.Pin_0
  N11: Arduino1.D4, R7.Pin_0
  N12: Arduino1.D3, R5.Pin_0
  N13: Arduino1.D2, part.Pin_0
  N14: Arduino1.+5V, part_3.Pin_1
  N15: R1.Pin_1, R2.Pin_1, R3.Pin_1, R4.Pin_1, R5.Pin_1, R6.Pin_1, R7.Pin_1, part.Pin_1, Audio-Output.Ring, Audio-Output.Tip
  N16: Midi_Input.5, part_4.Pin_0

notes:
  If you are using the MIDI Shield, this part is not required
